// Logisim project BOB-CPU.circ as structural Verilog: 1 circuit, main circuit BOB
module BOB (
  output [3:0] ZCOP,
  output [7:0] out_2,
  output [7:0] out_3
);

  wire CLK_out, cu_1_p3, cu_1_p4, cu_1_p6, cu_1_p7, cu_1_p8, cu_1_p9, not_1_out, not_2_out, not_3_out,
       pc_1_p4;
  wire [3:0] cu_1_p10, undriven;
  wire [7:0] cu_1_p5, multiplexer_1_out, pc_1_p6, ram_2_data, registers_1_p9, registers_1_p10;
  wire [15:0] pc_1_p3;

  Clock CLK (.out(CLK_out));
  // PC pc_1: pin names not known; wires that end beside it: CLK_out, out_2, pc_1_p3, pc_1_p4, ZCOP[3], pc_1_p6
  not not_1 (not_1_out, 1'b1);
  // CU cu_1: pin names not known; wires that end beside it: pc_1_p3, pc_1_p4, cu_1_p3, cu_1_p4, cu_1_p5, cu_1_p6, cu_1_p7, cu_1_p8, cu_1_p9, cu_1_p10
  RAM #(.dataWidth(16), .bus("separate")) ram_1 (
    .addr(pc_1_p6), .data(pc_1_p3), .str(not_1_out), .clk(CLK_out), .ld(1'b1));  // open: din, sel, clr
  not not_2 (not_2_out, cu_1_p4);
  Multiplexer #(.width(8)) multiplexer_1 (
    .in0(out_2), .in1(ram_2_data), .out(multiplexer_1_out), .sel(cu_1_p6));  // open: en
  RAM #(.bus("separate")) ram_2 (
    .addr(cu_1_p5), .din(out_3), .data(ram_2_data), .str(cu_1_p4), .clk(CLK_out), .ld(not_2_out));  // open: sel, clr
  not not_3 (not_3_out, cu_1_p4);
  // Registers registers_1: pin names not known; wires that end beside it: multiplexer_1_out, cu_1_p7, cu_1_p8, cu_1_p9, CLK_out, cu_1_p3, not_3_out, out_3, registers_1_p9, registers_1_p10
  Flags flags_1 (
    .ZCOP(undriven), .CLK(CLK_out), .PF__Parity_Flag(ZCOP[0]), .OF__Overflow_Flag(ZCOP[1]),
    .CF__Carry_Flag(ZCOP[2]), .ZF__Zero_Flag(ZCOP[3]));
  ALU alu_1 (
    .R1__Value_of_first_register(registers_1_p9), .R2__Value_of_second_register(registers_1_p10),
    .OUT__ALU_output(out_2), .COM__Value_of_command__0000_to_1111(cu_1_p10));  // open: FL__output_to_FLAG
endmodule
