// Logisim project CU.circ as structural Verilog: 2 circuits, main circuit main
// CU
module main (
  input  [15:0] INS__Instruction_value,
  output [3:0] COM__Value_of_command__0000_to_1111,
  output [2:0] A1__Adress_of_first_register,
  output [2:0] A2__Adress_of_second_register,
  output [7:0] MA__Adress_in_DATA_for_LOAD,
  output [2:0] DEST__Adress_of_register_that_loads_data,
  output L__if_1__input_from_DATA_to_REG_is_allowed,
  output J__if_1__JMP_is_allowed,
  output S__if_1__input_from_REG_to_DATA_is_allowed,
  output MV__if_1__transfer_data_within_REG_is_allowed
);

  wire and_2_out, or_2_out;

  PARSER parser_1 (
    .Instruction(INS__Instruction_value), .COM(COM__Value_of_command__0000_to_1111),
    .A1(A1__Adress_of_first_register), .A2(A2__Adress_of_second_register), .MA(MA__Adress_in_DATA_for_LOAD));
  and and_1 (MV__if_1__transfer_data_within_REG_is_allowed, ~COM__Value_of_command__0000_to_1111[3], ~COM__Value_of_command__0000_to_1111[2], ~COM__Value_of_command__0000_to_1111[1], ~COM__Value_of_command__0000_to_1111[0]);  // AND_Gate
  and and_2 (and_2_out, COM__Value_of_command__0000_to_1111[0], ~COM__Value_of_command__0000_to_1111[1], ~COM__Value_of_command__0000_to_1111[2], ~COM__Value_of_command__0000_to_1111[3]);  // AND_Gate
  or or_1 (L__if_1__input_from_DATA_to_REG_is_allowed, and_2_out, S__if_1__input_from_REG_to_DATA_is_allowed);
  and and_3 (S__if_1__input_from_REG_to_DATA_is_allowed, ~COM__Value_of_command__0000_to_1111[0], COM__Value_of_command__0000_to_1111[1], ~COM__Value_of_command__0000_to_1111[2], ~COM__Value_of_command__0000_to_1111[3]);  // AND_Gate
  and and_4 (J__if_1__JMP_is_allowed, ~COM__Value_of_command__0000_to_1111[0], COM__Value_of_command__0000_to_1111[1], COM__Value_of_command__0000_to_1111[2], ~COM__Value_of_command__0000_to_1111[3]);  // AND_Gate
  Multiplexer #(.width(3)) multiplexer_1 (
    .in0(A2__Adress_of_second_register), .in1(3'b000), .out(DEST__Adress_of_register_that_loads_data),
    .sel(or_2_out));  // open: en
  or or_2 (or_2_out, L__if_1__input_from_DATA_to_REG_is_allowed, S__if_1__input_from_REG_to_DATA_is_allowed);
endmodule

// PAR
module PARSER (
  input  [15:0] Instruction,
  output [3:0] COM,
  output [2:0] A1,
  output [2:0] A2,
  output [7:0] MA
);


  assign A1 = Instruction[6:4];
  assign A2 = Instruction[9:7];
  assign COM = Instruction[3:0];
  assign MA = Instruction[11:4];
endmodule
