// Logisim project Flags.circ as structural Verilog: 1 circuit, main circuit Flags
// FLAGS
module Flags (
  input  CLK,
  input  [3:0] ZCOE,
  output [3:0] ZCOE_out
);

  D_Flip_Flop ZF (.clk(CLK), .D(ZCOE[3]), .Q(ZCOE_out[3]));  // open: Qn, preset, en, reset
  D_Flip_Flop CF (.clk(CLK), .D(ZCOE[2]), .Q(ZCOE_out[2]));  // open: Qn, preset, en, reset
  D_Flip_Flop OF (.clk(CLK), .D(ZCOE[1]), .Q(ZCOE_out[1]));  // open: Qn, preset, en, reset
  D_Flip_Flop EF (.clk(CLK), .D(ZCOE[0]), .Q(ZCOE_out[0]));  // open: Qn, preset, en, reset
endmodule
