// Logisim project Registers.circ as structural Verilog: 2 circuits, main circuit Registers
// REG
module Registers (
  input  CLK,
  input  [7:0] SET,
  input  [2:0] ADRESS,
  input  Control,
  output [7:0] out_5
);

  wire not_1_out;
  wire [7:0] AX_q, BX_q, CX_q, demultiplexer_1_out0, demultiplexer_1_out1, demultiplexer_1_out2,
       demultiplexer_1_out3, demultiplexer_1_out4, demultiplexer_1_out5, demultiplexer_1_out6,
       demultiplexer_1_out7, DX_q, P1_q, P2_q, P3_q, PC_q;

  not not_1 (not_1_out, Control);
  Demultiplexer #(.select(3), .width(8)) demultiplexer_1 (
    .out0(demultiplexer_1_out0), .out1(demultiplexer_1_out1), .out2(demultiplexer_1_out2),
    .out3(demultiplexer_1_out3), .out4(demultiplexer_1_out4), .out5(demultiplexer_1_out5),
    .out6(demultiplexer_1_out6), .out7(demultiplexer_1_out7), .in(SET), .sel(ADRESS), .en(not_1_out));
  Register AX (.D(demultiplexer_1_out0), .Q(AX_q), .clk(CLK));  // open: en, clr
  Register BX (.D(demultiplexer_1_out1), .Q(BX_q), .clk(CLK));  // open: en, clr
  Register CX (.D(demultiplexer_1_out2), .Q(CX_q), .clk(CLK));  // open: en, clr
  Register DX (.D(demultiplexer_1_out3), .Q(DX_q), .clk(CLK));  // open: en, clr
  Register PC (.D(demultiplexer_1_out4), .Q(PC_q), .clk(CLK));  // open: en, clr
  Register P1 (.D(demultiplexer_1_out5), .Q(P1_q), .clk(CLK));  // open: en, clr
  Register P2 (.D(demultiplexer_1_out6), .Q(P2_q), .clk(CLK));  // open: en, clr
  Register P3 (.D(demultiplexer_1_out7), .Q(P3_q), .clk(CLK));  // open: en, clr
  Multiplexer #(.select(3), .width(8)) multiplexer_1 (
    .in0(AX_q), .in1(BX_q), .in2(CX_q), .in3(DX_q), .in4(PC_q), .in5(P1_q), .in6(P2_q), .in7(P3_q),
    .out(out_5), .sel(ADRESS), .en(Control));
endmodule

module stagdo (
  input  in_1
);

  Registers registers_1 ();  // open: SET, ADRESS, out_5, CLK, Control
endmodule
