// Logisim project procesor.circ as structural Verilog
module Procesor (
  output [3:0] ZCOP,
  output [7:0] out_2,
  output [7:0] out_3
);

  wire CLK_out, main_2_p2, main_2_p3, main_2_p4, main_2_p6, main_2_p7, main_2_p8, main_2_p9, not_1_out,
       not_2_out, not_3_out;
  wire [3:0] main_2_p10, undriven;
  wire [7:0] main_1_cl__current_line, main_2_p5, multiplexer_1_out, ram_2_data, registers_1_p9,
       registers_1_p10;
  wire [15:0] main_2_p1;

  Clock CLK (.out(CLK_out));
  PC_main main_1 (
    .CLK(CLK_out), .CL__current_line(main_1_cl__current_line), .JMP__Input_for_JMP_command(out_2),
    .CJ__if_1__JMP_is_allowed(ZCOP[3]), .J__if_1__JMP_is_allowed(main_2_p2));
  not not_1 (not_1_out, 1'b1);
  // CU_main main_2: pin names not known; wires that end beside it: main_2_p1, main_2_p2, main_2_p3, main_2_p4, main_2_p5, main_2_p6, main_2_p7, main_2_p8, main_2_p9, main_2_p10
  RAM #(.dataWidth(16), .bus("separate")) ram_1 (
    .addr(main_1_cl__current_line), .data(main_2_p1), .str(not_1_out), .clk(CLK_out), .ld(1'b1));  // open: din, sel, clr
  not not_2 (not_2_out, main_2_p4);
  Multiplexer #(.width(8)) multiplexer_1 (
    .in0(out_2), .in1(ram_2_data), .out(multiplexer_1_out), .sel(main_2_p6));  // open: en
  RAM #(.bus("separate")) ram_2 (
    .addr(main_2_p5), .din(out_3), .data(ram_2_data), .str(main_2_p4), .clk(CLK_out), .ld(not_2_out));  // open: sel, clr
  not not_3 (not_3_out, main_2_p4);
  // Registers registers_1: pin names not known; wires that end beside it: multiplexer_1_out, main_2_p7, main_2_p8, main_2_p9, CLK_out, main_2_p3, not_3_out, out_3, registers_1_p9, registers_1_p10
  Flags flags_1 (
    .ZCOP(undriven), .CLK(CLK_out), .PF__Parity_Flag(ZCOP[0]), .OF__Overflow_Flag(ZCOP[1]),
    .CF__Carry_Flag(ZCOP[2]), .ZF__Zero_Flag(ZCOP[3]));
  ALU alu_1 (
    .R1__Value_of_first_register(registers_1_p9), .R2__Value_of_second_register(registers_1_p10),
    .OUT__ALU_output(out_2), .COM__Value_of_command__0000_to_1111(main_2_p10));  // open: FLAGS_ZCOP
endmodule
